# Fritzing sketch SmartRoomController (saved by Fritzing 0.9.9b)
breadboards: 1

parts:
  S1 = Pushbutton [package="[THT]"]
  Teensy_3_2 = Teensy 3.1
  Water_Level_Sensor1 = Water Level Sensor
  R6 = Resistor [tolerance=±5% resistance=1k package="0805 [SMD]"]
  LED1 = smd LED [color="Red (633nm)" package="0603 [SMD]"]
  LED2 = smd LED [color="Green (555nm)" package="0603 [SMD]"]
  OLED_I2C1 = OLED 128x64 I2C Monochrome Display
  M1 = BMP280
  Mod1 = Passive Buzzer
  WIZ820io3 = WIZ820io [part_number=WIZ820io]
  R7 = Resistor [tolerance=±5% resistance=1k package="0805 [SMD]"]
  R8 = Resistor [tolerance=±5% resistance=1k package="0805 [SMD]"]

nets:
  N1: S1.Pin_1, S1.Pin_2, R6.Pin_1
  VIN: S1.Pin_3, S1.Pin_4, Teensy_3_2.3V3, OLED_I2C1.VDD, M1.VIN, Mod1.NC, WIZ820io3.VIN
  GND: Teensy_3_2.GND, Water_Level_Sensor1.GND, R6.Pin_0, OLED_I2C1.GND, M1.GND, Mod1.-, WIZ820io3.GND, R7.Pin_0, R8.Pin_0
  N2: Teensy_3_2.D3, LED2.anode
  N3: Teensy_3_2.D5, LED1.anode
  N4: Teensy_3_2.D9, WIZ820io3.nRESET
  N5: Teensy_3_2.D10, WIZ820io3.nSS
  N6: Teensy_3_2.D11, WIZ820io3.MOSI
  N7: Teensy_3_2.D12, WIZ820io3.MISO
  N8: Teensy_3_2.D13, WIZ820io3.SCLK
  N9: Teensy_3_2.A4/D18, OLED_I2C1.SDA
  N10: Teensy_3_2.A5/D19, OLED_I2C1.SCK
  N11: Teensy_3_2.A6/D20, Mod1.S
  N12: LED1.cathode, R7.Pin_1
  N13: LED2.cathode, R8.Pin_1

custom parts:
  Pushbutton: A generic pushbutton.
  Water Level Sensor: A water level sensor. This sensor operates at 3V to 5V. The Sig (signal) pin outputs an analogue signal that is in proportion to the amount of water in contact with the sensor.
  BMP280: Temperature Humidity Barometric presure Sensor, I2C
